# Fritzing sketch pinokia (saved by Fritzing 0.7.11b)

parts:
  Part1 = Arduino Color LCD Shield
  RaspberryPi1 = Raspberry_Pi_Model_B

nets:
  N1: Part1.D13, RaspberryPi1.connector23
  N2: Part1.D11, RaspberryPi1.connector19
  N3: Part1.D9, RaspberryPi1.connector24
  N4: Part1.D8, RaspberryPi1.connector22
  N5: Part1.GND, RaspberryPi1.connector6
  N6: Part1.5V, RaspberryPi1.connector2
  N7: Part1.3.3V, RaspberryPi1.connector1
