# Fritzing sketch pinokia (saved by Fritzing 0.7.11b)

parts:
  Part1 = Arduino Color LCD Shield
  RaspberryPi1 = Raspberry Pi Model B

nets:
  N1: Part1.D13, RaspberryPi1.SCLK
  N2: Part1.D11, RaspberryPi1.MOSI
  N3: Part1.D9, RaspberryPi1.CS0
  N4: Part1.D8, RaspberryPi1.#25
  GND: Part1.GND, RaspberryPi1.GND
  5V: Part1.5V, RaspberryPi1.5V
  3.3V: Part1.3.3V, RaspberryPi1.3V3

custom parts:
  Raspberry Pi Model B: Raspberry Pi (Model B)
